// Logisim project ALU.circ as structural Verilog: 1 circuit, main circuit ALU
module ALU (
  input  [31:0] A,
  input  [31:0] B,
  input  [4:0] Shift,
  input  [3:0] Codop,
  input  CarryIn,
  input  [4:0] MenosUno,
  output [3:0] Flags,
  output [31:0] S
);

  wire and_4_out, and_5_out, and_6_out, and_7_out, bitselector_5_out, bitselector_6_out, bitselector_7_out,
       bitselector_8_out, bitselector_9_out, bitselector_10_out, bitselector_11_out, bitselector_12_out,
       C_ADC, C_ASR, C_CMN, C_CMP, C_LSL, C_LSR, C_ROR, C_SBC, CALC_V_ADD, CALC_V_SUB, not_1_out, not_6_out,
       not_7_out, not_8_out, not_9_out, not_10_out, not_11_out, subtractor_3_bout, subtractor_5_bout,
       V_DEF_ADD, V_DEF_SUB;
  wire [4:0] SELECT_LSL, SLCT_LSR_ASR;
  wire [31:0] A_ND, ADC, ASR, BIC, CMN, CMP, EOR, LSL, LSR, MUL, multiplexer_3_out, MVN, not_4_out, ORR,
       R_OR, RSB, SBC, TST;

  Subtractor #(.width(5)) subtractor_1 (.a({5{1'b0}}), .b(Shift), .out(SELECT_LSL));  // open: bin, bout
  Subtractor #(.width(5)) subtractor_2 (.a(Shift), .b(MenosUno), .out(SLCT_LSR_ASR));  // open: bin, bout
  assign A_ND = A & B;  // AND_Gate and_1, 32 bits wide
  assign EOR = A ^ B;  // XOR_Gate xor_1, 32 bits wide
  BitSelector #(.width(32)) bitselector_1 (.in(B), .out(C_LSL), .sel(SELECT_LSL));
  Shifter #(.width(32)) shifter_1 (.in(B), .\dist (Shift), .out(LSL));
  BitSelector #(.width(32)) bitselector_2 (.in(B), .out(C_LSR), .sel(SLCT_LSR_ASR));
  Shifter #(.shift("lr"), .width(32)) shifter_2 (.in(B), .\dist (Shift), .out(LSR));
  BitSelector #(.width(32)) bitselector_3 (.in(B), .out(C_ASR), .sel(SLCT_LSR_ASR));
  Shifter #(.shift("ar"), .width(32)) shifter_3 (.in(B), .\dist (Shift), .out(ASR));
  Adder #(.width(32)) adder_1 (.a(A), .b(B), .out(ADC), .cin(CarryIn), .cout(C_ADC));
  not not_1 (not_1_out, CarryIn);
  Subtractor #(.width(32)) subtractor_3 (.a(B), .b(A), .out(SBC), .bin(not_1_out), .bout(subtractor_3_bout));
  not not_2 (C_SBC, subtractor_3_bout);
  Shifter #(.shift("rr"), .width(32)) shifter_4 (.in(B), .\dist (Shift), .out(R_OR));
  BitSelector #(.width(32)) bitselector_4 (.in(R_OR), .out(C_ROR), .sel({5{1'b1}}));
  assign TST = A & B;  // AND_Gate and_2, 32 bits wide
  Subtractor #(.width(32)) subtractor_4 (.a({32{1'b0}}), .b(A), .out(RSB));  // open: bin, bout
  Subtractor #(.width(32)) subtractor_5 (.a(B), .b(A), .out(CMP), .bout(subtractor_5_bout));  // open: bin
  not not_3 (C_CMP, subtractor_5_bout);
  Adder #(.width(32)) adder_2 (.a(B), .b(A), .out(CMN), .cout(C_CMN));  // open: cin
  assign ORR = B | A;  // OR_Gate or_1, 32 bits wide
  Multiplier #(.width(32)) multiplier_1 (.a(B), .b(A), .out(MUL));  // open: cin, cout
  assign BIC = B & not_4_out;  // AND_Gate and_3, 32 bits wide
  assign not_4_out = ~A;  // NOT_Gate not_4, 32 bits wide
  assign MVN = ~A;  // NOT_Gate not_5, 32 bits wide
  BitSelector #(.width(32)) bitselector_5 (.in(ADC), .out(bitselector_5_out), .sel({5{1'b1}}));
  BitSelector #(.width(32)) bitselector_6 (.in(CMN), .out(bitselector_6_out), .sel({5{1'b1}}));
  BitSelector #(.width(32)) bitselector_7 (.in(SBC), .out(bitselector_7_out), .sel({5{1'b1}}));
  BitSelector #(.width(32)) bitselector_8 (.in(CMP), .out(bitselector_8_out), .sel({5{1'b1}}));
  BitSelector #(.width(32)) bitselector_9 (.in(B), .out(bitselector_9_out), .sel({5{1'b1}}));
  BitSelector #(.width(32)) bitselector_10 (.in(B), .out(bitselector_10_out), .sel({5{1'b1}}));
  Multiplexer #(.select(4)) multiplexer_1 (
    .in0(1'b0), .in1(1'b0), .in2(1'b0), .in3(1'b0), .in4(1'b0), .in5(bitselector_5_out), .in6(1'b0),
    .in7(1'b0), .in8(1'b0), .in9(1'b0), .in10(1'b0), .in11(bitselector_6_out), .in12(1'b0), .in13(1'b0),
    .in14(1'b0), .in15(1'b0), .out(CALC_V_ADD), .sel(Codop));
  Multiplexer #(.select(4)) multiplexer_2 (
    .in0(1'b0), .in1(1'b0), .in2(1'b0), .in3(1'b0), .in4(1'b0), .in5(1'b0), .in6(bitselector_7_out),
    .in7(1'b0), .in8(1'b0), .in9(1'b0), .in10(bitselector_8_out), .in11(1'b0), .in12(1'b0), .in13(1'b0),
    .in14(1'b0), .in15(1'b0), .out(CALC_V_SUB), .sel(Codop));
  not not_6 (not_6_out, bitselector_9_out);
  not not_7 (not_7_out, bitselector_11_out);
  BitSelector #(.width(32)) bitselector_11 (.in(A), .out(bitselector_11_out), .sel({5{1'b1}}));
  not not_8 (not_8_out, CALC_V_ADD);
  not not_9 (not_9_out, bitselector_10_out);
  BitSelector #(.width(32)) bitselector_12 (.in(A), .out(bitselector_12_out), .sel({5{1'b1}}));
  not not_10 (not_10_out, bitselector_12_out);
  not not_11 (not_11_out, CALC_V_SUB);
  and and_4 (and_4_out, CALC_V_ADD, not_6_out, not_7_out);
  and and_5 (and_5_out, bitselector_11_out, bitselector_9_out, not_8_out);
  and and_6 (and_6_out, CALC_V_SUB, not_9_out, bitselector_12_out);
  and and_7 (and_7_out, not_10_out, bitselector_10_out, not_11_out);
  or or_2 (V_DEF_ADD, and_4_out, and_5_out);
  or or_3 (V_DEF_SUB, and_6_out, and_7_out);
  Multiplexer #(.select(4), .width(32)) multiplexer_3 (
    .in0(A_ND), .in1(EOR), .in2(LSL), .in3(LSR), .in4(ASR), .in5(ADC), .in6(SBC), .in7(R_OR), .in8(TST),
    .in9(RSB), .in10(CMP), .in11(CMN), .in12(ORR), .in13(MUL), .in14(BIC), .in15(MVN),
    .out(multiplexer_3_out), .sel(Codop));
  Multiplexer #(.select(4)) multiplexer_4 (
    .in0(1'b0), .in1(1'b0), .in2(C_LSL), .in3(C_LSR), .in4(C_ASR), .in5(C_ADC), .in6(C_SBC), .in7(C_ROR),
    .in8(1'b0), .in9(1'b0), .in10(C_CMP), .in11(C_CMN), .in12(1'b0), .in13(1'b0), .in14(1'b0), .in15(1'b0),
    .out(Flags[1]), .sel(Codop));
  Multiplexer #(.select(4)) multiplexer_5 (
    .in0(1'b0), .in1(1'b0), .in2(1'b0), .in3(1'b0), .in4(1'b0), .in5(V_DEF_ADD), .in6(V_DEF_SUB), .in7(1'b0),
    .in8(1'b0), .in9(V_DEF_SUB), .in10(V_DEF_SUB), .in11(V_DEF_ADD), .in12(1'b0), .in13(1'b0), .in14(1'b0),
    .in15(1'b0), .out(Flags[0]), .sel(Codop));
  Comparator #(.width(32)) comparator_1 (
    .a(multiplexer_3_out), .b({32{1'b0}}), .eq(Flags[2]), .lt(Flags[3]));  // open: gt
  Multiplexer #(.select(4), .width(32)) multiplexer_6 (
    .in0(multiplexer_3_out), .in1(multiplexer_3_out), .in2(multiplexer_3_out), .in3(multiplexer_3_out),
    .in4(multiplexer_3_out), .in5(multiplexer_3_out), .in6(multiplexer_3_out), .in7(multiplexer_3_out),
    .in8(B), .in9(multiplexer_3_out), .in10(B), .in11(B), .in12(multiplexer_3_out), .in13(multiplexer_3_out),
    .in14(multiplexer_3_out), .in15(multiplexer_3_out), .out(S), .sel(Codop));

  // Other names for the same wires on the sheet: CARRY = CarryIn; V = Flags[0]; C = Flags[1]; Z = Flags[2];
  //   N = Flags[3]; SORTIE[31:0] = S

  // Notes on the sheet:
  //   MenosUno: initial=0x1
  //   Codop: initial=0x11
  //   Shift: initial=0x26
  //   Note: for ROR, C = N
  //   Note 2: assume that shift > 0 for LSL and LSR
  //   Pas d'overflow pour RSB
endmodule
