// Logisim project Ctl_Conditional.circ as structural Verilog: 1 circuit, main circuit Conditional
module Conditional (
  input  Enable,
  input  [15:0] Instruction,
  input  Z,
  input  C,
  input  N,
  input  V,
  output [10:0] Offset,
  output Verified
);

  wire and_3_out, bitselector_1_out, bitselector_2_out, GT, HI, LE, LS, LT, multiplexer_2_out, not_1_out,
       not_2_out, not_3_out, not_4_out, not_5_out, not_6_out, not_7_out, not_8_out, not_9_out;
  wire [10:0] bit_extender_1_out, Offset_t;

  not not_1 (not_1_out, LT);
  not not_2 (not_2_out, N);
  not not_3 (not_3_out, V);
  and and_1 (HI, C, not_4_out);
  not not_4 (not_4_out, Z);
  not not_5 (not_5_out, C);
  or or_1 (LS, not_5_out, Z);
  not not_6 (not_6_out, Z);
  and and_2 (GT, not_6_out, LT);
  or or_2 (LE, Z, not_1_out);
  not not_7 (not_7_out, C);
  BitSelector #(.width(16)) bitselector_1 (.in(Instruction), .out(bitselector_1_out), .sel(4'b1100));
  xnor xnor_1 (LT, N, V);
  not not_8 (not_8_out, Z);
  not not_9 (not_9_out, LT);
  assign bit_extender_1_out = {{3{Instruction[7]}}, Instruction[7:0]};  // Bit_Extender bit_extender_1
  Multiplexer #(.width(11)) multiplexer_1 (
    .in0(Instruction[10:0]), .in1(bit_extender_1_out), .out(Offset_t), .sel(bitselector_1_out));
  Multiplexer #(.select(4)) multiplexer_2 (
    .in0(Z), .in1(not_8_out), .in2(C), .in3(not_7_out), .in4(N), .in5(not_2_out), .in6(V), .in7(not_3_out),
    .in8(HI), .in9(LS), .in10(LT), .in11(not_9_out), .in12(GT), .in13(LE), .in14(1'b1), .in15(1'b0),
    .out(multiplexer_2_out), .sel(Instruction[11:8]));
  and and_3 (and_3_out, Enable, multiplexer_2_out);
  BitSelector #(.width(16)) bitselector_2 (.in(Instruction), .out(bitselector_2_out), .sel(4'b1100));
  Multiplexer #(.width(11)) multiplexer_3 (.in0({11{1'b0}}), .in1(Offset_t), .out(Offset), .sel(Enable));
  Multiplexer multiplexer_4 (.in0(Enable), .in1(and_3_out), .out(Verified), .sel(bitselector_2_out));

  // Other names for the same wires on the sheet: Imm8[7:0] = Instruction[7:0]; cond[3:0] = Instruction[11:8]
endmodule
