// Logisim project Ctl_Data_Processing.circ as structural Verilog: 1 circuit, main circuit Data_Processing
module Data_Processing (
  input  [15:0] Instruction,
  input  Enable,
  output [2:0] Rd,
  output [2:0] Rn,
  output [2:0] Rm,
  output [3:0] ALU_Opcode,
  output [3:0] Flags_Update_Mask
);

  wire [2:0] Rd_t, Rm_t, Rn_t;
  wire [3:0] Flag;

  Multiplexer #(.select(4), .width(4)) multiplexer_1 (
    .in0(4'b0011), .in1(4'b0011), .in2(4'b1011), .in3(4'b1011), .in4(4'b1011), .in5(4'b1111), .in6(4'b0111),
    .in7(4'b1011), .in8(4'b1111), .in9(4'b0111), .in10(4'b1111), .in11(4'b1111), .in12(4'b0011),
    .in13(4'b0011), .in14(4'b0011), .in15(4'b0011), .out(Flag), .sel(Instruction[9:6]));
  Multiplexer #(.select(4), .width(3)) multiplexer_2 (
    .in0(Instruction[2:0]), .in1(Instruction[2:0]), .in2(Instruction[2:0]), .in3(Instruction[2:0]),
    .in4(Instruction[2:0]), .in5(Instruction[2:0]), .in6(Instruction[2:0]), .in7(Instruction[2:0]),
    .in8(3'b000), .in9(Instruction[2:0]), .in10(Instruction[2:0]), .in11(3'b000), .in12(Instruction[2:0]),
    .in13(Instruction[2:0]), .in14(Instruction[2:0]), .in15(Instruction[2:0]), .out(Rd_t),
    .sel(Instruction[9:6]));
  Multiplexer #(.select(4), .width(3)) multiplexer_3 (
    .in0(Instruction[2:0]), .in1(Instruction[2:0]), .in2(Instruction[2:0]), .in3(Instruction[2:0]),
    .in4(Instruction[2:0]), .in5(Instruction[2:0]), .in6(Instruction[2:0]), .in7(Instruction[2:0]),
    .in8(Instruction[2:0]), .in9(Instruction[5:3]), .in10(Instruction[2:0]), .in11(Instruction[2:0]),
    .in12(Instruction[2:0]), .in13(Instruction[5:3]), .in14(Instruction[2:0]), .in15(3'b000), .out(Rn_t),
    .sel(Instruction[9:6]));
  Multiplexer #(.select(4), .width(3)) multiplexer_4 (
    .in0(Instruction[5:3]), .in1(Instruction[5:3]), .in2(Instruction[5:3]), .in3(Instruction[5:3]),
    .in4(Instruction[5:3]), .in5(Instruction[5:3]), .in6(Instruction[5:3]), .in7(Instruction[5:3]),
    .in8(Instruction[5:3]), .in9(Instruction[5:3]), .in10(Instruction[5:3]), .in11(Instruction[5:3]),
    .in12(Instruction[5:3]), .in13(Instruction[2:0]), .in14(Instruction[5:3]), .in15(Instruction[5:3]),
    .out(Rm_t), .sel(Instruction[9:6]));
  Multiplexer #(.width(3)) multiplexer_5 (.in0(3'b000), .in1(Rd_t), .out(Rd), .sel(Enable));
  Multiplexer #(.width(3)) multiplexer_6 (.in0(3'b000), .in1(Rn_t), .out(Rn), .sel(Enable));
  Multiplexer #(.width(3)) multiplexer_7 (.in0(3'b000), .in1(Rm_t), .out(Rm), .sel(Enable));
  Multiplexer #(.width(4)) multiplexer_8 (.in0(4'b0000), .in1(Instruction[9:6]), .out(ALU_Opcode), .sel(Enable));
  Multiplexer #(.width(4)) multiplexer_9 (.in0(4'b0000), .in1(Flag), .out(Flags_Update_Mask), .sel(Enable));

  // Other names for the same wires on the sheet: En = Enable; OperandDroite[2:0] = Instruction[2:0];
  //   OperandGauche[2:0] = Instruction[5:3]; ALU[3:0] = Instruction[9:6]
endmodule
