// Logisim project Ctl_Flags_APSR.circ as structural Verilog: 1 circuit, main circuit Flags_APSR
module Flags_APSR (
  input  [3:0] Update_Mask,
  input  [3:0] Flags_In,
  input  Clk,
  input  Rst,
  output [3:0] Flags_Out
);

  Register #(.width(1)) register_1 (.D(Flags_In[3]), .en(Update_Mask[3]), .clk(Clk), .Q(Flags_Out[3]), .clr(Rst));
  Register #(.width(1)) register_2 (.D(Flags_In[2]), .en(Update_Mask[2]), .clk(Clk), .Q(Flags_Out[2]), .clr(Rst));
  Register #(.width(1)) register_3 (.D(Flags_In[1]), .en(Update_Mask[1]), .clk(Clk), .Q(Flags_Out[1]), .clr(Rst));
  Register #(.width(1)) register_4 (.D(Flags_In[0]), .en(Update_Mask[0]), .clk(Clk), .Q(Flags_Out[0]), .clr(Rst));

  // Other names for the same wires on the sheet: V = Flags_In[0]; C = Flags_In[1]; Z = Flags_In[2]; N = Flags_In[3];
  //   V_Udp = Flags_Out[0]; C_Udp = Flags_Out[1]; Z_Udp = Flags_Out[2]; N_Udp = Flags_Out[3];
  //   V_IsUpdt = Update_Mask[0]; C_IsUpdt = Update_Mask[1]; Z_IsUpdt = Update_Mask[2]; N_IsUpdt = Update_Mask[3]
endmodule
