// Logisim project Ctl_Load_Store.circ as structural Verilog: 1 circuit, main circuit Load_Store
module Load_Store (
  input  Enable,
  input  Clk,
  input  Reset,
  input  [31:0] Stack_Pointer,
  input  [15:0] Instruction,
  output Store,
  output Load,
  output PC_Hold,
  output [2:0] Rmd,
  output [31:0] RAM_Addr
);

  wire multiplexer_1_out, multiplexer_2_out;
  wire [31:0] bit_extender_1_out, CalcRam, multiplier_1_out, undriven;

  assign bit_extender_1_out = {{24{1'b0}}, Instruction[7:0]};  // Bit_Extender bit_extender_1
  Multiplier #(.width(32)) multiplier_1 (.a(bit_extender_1_out), .b(32'h4), .out(multiplier_1_out));  // open: cin, cout
  D_Flip_Flop d_ff_1 ();  // open: D, clk, Q, Qn, preset, reset
  Adder #(.width(32)) adder_1 (.a(multiplier_1_out), .b(Stack_Pointer), .out(CalcRam));  // open: cin, cout
  Multiplexer multiplexer_1 (.in0(1'b1), .in1(1'b0), .out(multiplexer_1_out), .sel(Instruction[11]));
  Multiplexer multiplexer_2 (.in0(1'b0), .in1(1'b1), .out(multiplexer_2_out), .sel(Instruction[11]));
  Multiplexer #(.width(3)) multiplexer_3 (.in0(3'b000), .in1(Instruction[10:8]), .out(Rmd), .sel(Enable));
  Multiplexer multiplexer_4 (.in0(1'b0), .in1(multiplexer_1_out), .out(Store), .sel(Enable));
  Multiplexer multiplexer_5 (.in0(1'b0), .in1(multiplexer_2_out), .out(Load), .sel(Enable));
  Multiplexer multiplexer_6 (.in0(1'b0), .out(PC_Hold), .sel(Enable));  // open: in1
  Multiplexer #(.width(32)) multiplexer_7 (.in0({32{1'b0}}), .in1(undriven), .out(RAM_Addr), .sel(Enable));

  // Other names for the same wires on the sheet: Clock = Clk; Imm8[7:0] = Instruction[7:0];
  //   Rdm[2:0] = Instruction[10:8]; Store_or_Load = Instruction[11]; Sp[31:0] = Stack_Pointer

  // Notes on the sheet:
  //   Delay load and hold PC for 1 cycle for the RAM to send out requested data 
endmodule
