// Logisim project Ctl_Opcode_Decoder.circ as structural Verilog: 1 circuit, main circuit Opcode_Decoder
module Opcode_Decoder (
  input  [5:0] Opcode,
  output Shift,
  output Data_Processing,
  output Load_Store,
  output SP_Address,
  output Conditional
);

  wire not_1_out, not_2_out, not_3_out, not_4_out, not_5_out, not_6_out;

  not not_1 (not_1_out, Opcode[5]);
  not not_2 (not_2_out, Opcode[4]);
  not not_3 (not_3_out, Opcode[5]);
  and and_1 (Shift, not_1_out, not_2_out);
  and and_2 (Data_Processing, not_3_out, Opcode[4]);
  and and_3 (Conditional, Opcode[5], Opcode[4]);
  not not_4 (not_4_out, Opcode[4]);
  and and_4 (Load_Store, Opcode[5], not_4_out, not_5_out);
  not not_5 (not_5_out, Opcode[3]);
  not not_6 (not_6_out, Opcode[4]);
  and and_5 (SP_Address, Opcode[5], not_6_out, Opcode[3]);

  // Other names for the same wires on the sheet: isCond = Conditional; isData = Data_Processing; isLoad = Load_Store;
  //   isShift = Shift; isStack = SP_Address; Bit3 = Opcode[3]; Bit4 = Opcode[4]; Bit5 = Opcode[5]

  // Notes on the sheet:
  //   Data Processing
  //   Shift, add, sub, mov
  //   Conditional branch
  //   Load/Store
  //   SP Address
  //   Shift, add, sub, mov
  //   Load/Store
  //   SP Address
  //   Data Processing
  //   Conditional branch
endmodule
