// Logisim project Ctl_Shift_Add_Sub_Mov.circ as structural Verilog: 1 circuit, main circuit Shift_Add_Sub_Mov
module Shift_Add_Sub_Mov (
  input  Enable,
  input  [15:0] Instruction,
  output [3:0] Flags_Update_Mask,
  output Carry,
  output Imm32_Enable,
  output [2:0] Rm,
  output [2:0] Rn,
  output [2:0] Rd,
  output [4:0] Imm5,
  output [31:0] Imm32,
  output [3:0] ALU_Opcode
);

  wire and_4_out, and_5_out, and_6_out, and_7_out, and_9_out, and_14_out, and_15_out, is_ADD, is_ADD_or_SUB,
       is_ADD_or_SUB_imm, is_ASRS, is_CMP, is_imm, is_LS, is_LSLS, is_LSRS, is_MOVS, is_Shift, is_SUB,
       not_1_out, not_2_out, not_3_out, not_4_out, not_5_out, not_6_out, not_7_out, not_8_out, not_9_out,
       not_10_out, or_1_out, or_5_out;
  wire [2:0] multiplexer_14_out, multiplexer_16_out;
  wire [3:0] multiplexer_1_out, multiplexer_3_out, multiplexer_4_out, multiplexer_5_out, multiplexer_6_out,
       multiplexer_7_out, multiplexer_8_out, multiplexer_19_out;
  wire [31:0] adder_1_out, Ainverser, not_11_out, Traite;

  not not_1 (not_1_out, Instruction[12]);
  not not_2 (not_2_out, Instruction[13]);
  not not_3 (not_3_out, Instruction[11]);
  not not_4 (not_4_out, Instruction[13]);
  and and_1 (is_ADD_or_SUB, Instruction[11], Instruction[12]);
  not not_5 (not_5_out, Instruction[11]);
  not not_6 (not_6_out, Instruction[11]);
  not not_7 (not_7_out, Instruction[12]);
  not not_8 (not_8_out, Instruction[12]);
  and and_2 (is_LS, not_1_out, not_2_out);
  and and_3 (is_ASRS, not_3_out, and_4_out);
  and and_4 (and_4_out, Instruction[12], not_4_out);
  and and_5 (and_5_out, not_5_out, Instruction[12]);
  and and_6 (and_6_out, not_7_out, Instruction[13]);
  and and_7 (and_7_out, not_8_out, Instruction[13]);
  not not_9 (not_9_out, Instruction[11]);
  and and_8 (is_SUB, is_ADD_or_SUB, or_1_out);
  or or_1 (or_1_out, Instruction[9], Instruction[13]);
  or or_2 (is_ADD, is_ADD_or_SUB, and_9_out);
  and and_9 (and_9_out, and_5_out, Instruction[13]);
  and and_10 (is_MOVS, not_6_out, and_6_out);
  and and_11 (is_CMP, Instruction[11], and_7_out);
  and and_12 (is_LSLS, not_9_out, is_LS);
  and and_13 (is_LSRS, Instruction[11], is_LS);
  or or_3 (is_Shift, is_LS, is_ASRS);
  and and_14 (and_14_out, Instruction[10], Instruction[11]);
  and and_15 (and_15_out, Instruction[12], not_10_out);
  not not_10 (not_10_out, Instruction[13]);
  and and_16 (is_ADD_or_SUB_imm, and_14_out, and_15_out);
  assign not_11_out = ~Ainverser;  // NOT_Gate not_11, 32 bits wide
  Adder #(.width(32)) adder_1 (.a(not_11_out), .b(32'h1), .out(adder_1_out));  // open: cin, cout
  Multiplexer #(.width(4)) multiplexer_1 (.in0(4'b1010), .in1(4'b1001), .out(multiplexer_1_out), .sel(is_MOVS));
  Multiplexer #(.width(32)) multiplexer_2 (.in0(Ainverser), .in1(adder_1_out), .out(Traite), .sel(is_MOVS));
  Multiplexer #(.width(4)) multiplexer_3 (
    .in0(multiplexer_1_out), .in1(4'b0101), .out(multiplexer_3_out), .sel(is_ADD));
  Multiplexer #(.width(4)) multiplexer_4 (
    .in0(multiplexer_3_out), .in1(4'b0110), .out(multiplexer_4_out), .sel(is_SUB));
  Multiplexer #(.width(4)) multiplexer_5 (.in0(4'b1111), .in1(4'b1110), .out(multiplexer_5_out), .sel(is_Shift));
  or or_4 (is_imm, is_ADD_or_SUB_imm, Instruction[13]);
  Multiplexer #(.width(4)) multiplexer_6 (
    .in0(multiplexer_4_out), .in1(4'b0100), .out(multiplexer_6_out), .sel(is_ASRS));
  Multiplexer #(.width(4)) multiplexer_7 (
    .in0(multiplexer_5_out), .in1(4'b1100), .out(multiplexer_7_out), .sel(is_MOVS));
  Multiplexer #(.width(4)) multiplexer_8 (
    .in0(multiplexer_6_out), .in1(4'b0011), .out(multiplexer_8_out), .sel(is_LSRS));
  Multiplexer #(.width(4)) multiplexer_9 (
    .in0(4'b0000), .in1(multiplexer_7_out), .out(Flags_Update_Mask), .sel(Enable));
  Multiplexer multiplexer_10 (.in0(1'b0), .in1(or_5_out), .out(Carry), .sel(Enable));
  or or_5 (or_5_out, is_SUB, is_CMP);
  Multiplexer multiplexer_11 (.in0(1'b0), .in1(is_imm), .out(Imm32_Enable), .sel(Enable));
  Multiplexer #(.width(3)) multiplexer_12 (.in0(3'b000), .in1(Instruction[8:6]), .out(Rm), .sel(Enable));
  Multiplexer #(.width(3)) multiplexer_13 (.in0(3'b000), .in1(multiplexer_14_out), .out(Rn), .sel(Enable));
  Multiplexer #(.width(3)) multiplexer_14 (
    .in0(Instruction[5:3]), .in1(Instruction[10:8]), .out(multiplexer_14_out), .sel(Instruction[13]));
  Multiplexer #(.width(3)) multiplexer_15 (.in0(3'b000), .in1(multiplexer_16_out), .out(Rd), .sel(Enable));
  Multiplexer #(.width(3)) multiplexer_16 (
    .in0(Instruction[2:0]), .in1(Instruction[10:8]), .out(multiplexer_16_out), .sel(Instruction[13]));
  Multiplexer #(.width(5)) multiplexer_17 (.in0({5{1'b0}}), .in1(Instruction[10:6]), .out(Imm5), .sel(Enable));
  Multiplexer #(.width(32)) multiplexer_18 (
    .in0({{29{1'b0}}, Instruction[8:6]}), .in1({{24{1'b0}}, Instruction[7:0]}), .out(Ainverser),
    .sel(Instruction[13]));
  Multiplexer #(.width(4)) multiplexer_19 (
    .in0(multiplexer_8_out), .in1(4'b0010), .out(multiplexer_19_out), .sel(is_LSLS));
  Multiplexer #(.width(4)) multiplexer_20 (.in0(4'b0000), .in1(multiplexer_19_out), .out(ALU_Opcode), .sel(Enable));
  Multiplexer #(.width(32)) multiplexer_21 (.in0({32{1'b0}}), .in1(Traite), .out(Imm32), .sel(Enable));

  // Other names for the same wires on the sheet: bits_10_0[10:0] = Instruction[10:0]; imm5_t[4:0] = Instruction[10:6];
  //   Rdn[2:0] = Instruction[10:8]; Rm_imm3[2:0] = Instruction[8:6]; imm8[7:0] = Instruction[7:0];
  //   Rd_bits_2_0[2:0] = Instruction[2:0]; Rn_t[2:0] = Instruction[5:3]; is_b10 = Instruction[10];
  //   is_b11 = Instruction[11]; Operande[2:0] = Instruction[13:11]; is_b12 = Instruction[12];
  //   is_b13 = Instruction[13]

  // Notes on the sheet:
  //   Note: ALU uses Rn register for shifts. Use Rn instead of Rm for shifts (immediate) here too
  //   Note 3: Imm32_Enable forces the use of the immediate for Rm register
  //   Note 2: MOV uses RSB ALU opcode with Imm8 reversed so that it is copied to output register
  //   Pull output low on Enable = 0
  //   CMP
  //   only ADD and SUB use Rm
  //   Enable carry for SUB since it is reversed in ALU
  //   ALU will use Imm32 instead of Rm
endmodule
